// Logisim project ADD_1.circ as structural Verilog: 2 circuits, main circuit main
module main (
  input  A,
  input  B,
  input  VEM_1,
  output VAI_1,
  output S
);

  ADD_1 add_1_1 (.S(S), .Vai_1(VAI_1), .A(A), .B(B), .C(VEM_1));
endmodule

module ADD_1 (
  input  A,
  input  B,
  input  C,
  output S,
  output Vai_1
);

  wire and_1_out, and_2_out, or_1_out, xor_1_out;

  xor xor_1 (xor_1_out, C, B);
  or or_1 (or_1_out, C, B);
  xor xor_2 (S, xor_1_out, A);
  and and_1 (and_1_out, or_1_out, A);
  and and_2 (and_2_out, C, B);
  or or_2 (Vai_1, and_1_out, and_2_out);
endmodule
