// Logisim project ADD_4.circ as structural Verilog: 3 circuits, main circuit main
module main (
  input  A,
  input  B,
  input  [3:0] A_2,
  input  [3:0] B_2,
  input  VEM_1,
  output VAI_1,
  output out_7,
  output S,
  output [3:0] out_9
);

  ADD_1 add_1_1 (.S(S), .Vai_1(VAI_1), .A(A), .B(B), .C(VEM_1));
  add_4 add_4_1 (.in_2(A_2), .Overflow(out_7), .in_1(B_2), .out_4(out_9));
endmodule

module ADD_1 (
  input  A,
  input  B,
  input  C,
  output S,
  output Vai_1
);

  wire and_1_out, and_2_out, or_1_out, xor_1_out;

  xor xor_1 (xor_1_out, C, B);
  or or_1 (or_1_out, C, B);
  xor xor_2 (S, xor_1_out, A);
  and and_1 (and_1_out, or_1_out, A);
  and and_2 (and_2_out, C, B);
  or or_2 (Vai_1, and_1_out, and_2_out);
endmodule

module add_4 (
  input  [3:0] in_1,
  input  [3:0] in_2,
  output Overflow,
  output [3:0] out_4
);

  wire add_1_2_vai_1, add_1_3_vai_1, add_1_4_vai_1;

  ADD_1 add_1_1 (.S(out_4[3]), .Vai_1(Overflow), .A(in_2[3]), .B(in_1[3]), .C(add_1_2_vai_1));
  ADD_1 add_1_2 (.S(out_4[2]), .Vai_1(add_1_2_vai_1), .A(in_2[2]), .B(in_1[2]), .C(add_1_3_vai_1));
  ADD_1 add_1_3 (.S(out_4[1]), .Vai_1(add_1_3_vai_1), .A(in_2[1]), .B(in_1[1]), .C(add_1_4_vai_1));
  ADD_1 add_1_4 (.S(out_4[0]), .Vai_1(add_1_4_vai_1), .A(in_2[0]), .B(in_1[0]), .C(1'b0));
endmodule
