// Logisim project Rot_Dir.circ as structural Verilog: 7 circuits, main circuit main
module main (
  input  [3:0] A,
  input  [3:0] B,
  input  A_2,
  input  B_2,
  input  C,
  input  [3:0] B_3,
  input  [3:0] A_3,
  input  [1:0] x_y,
  output VAI_1,
  output Overflow,
  output S,
  output [3:0] S_2,
  output Overflow_2,
  output Overflow_3,
  output [3:0] S_3,
  output [3:0] S_4,
  output [3:0] S_5,
  output [3:0] S_6
);

  ADD_1 add_1_1 (.S(S), .Vai_1(VAI_1), .A(A_2), .B(B_2), .C(C));
  ADD_4 add_4_1 (.A(A_3), .Overflow(Overflow_2), .B(B_3), .S(S_5));
  SUB_4 sub_4_1 (.A(A_3), .Overflow(Overflow_3), .B(B_3), .S(S_6));
  ADD_4 add_4_2 (.A(A), .Overflow(Overflow), .B(B), .S(S_2));
  // Probe on S_6
  Rot_esq rot_esq_1 (.a_b_c_d(A_3), .x_y(x_y), .A__B_C_D(S_3));
  Rot_dir rot_dir_1 (.a_b_c_d(A_3), .in_2(x_y), .A_B_C_D_2(S_4));
endmodule

module ADD_1 (
  input  A,
  input  B,
  input  C,
  output S,
  output Vai_1
);

  wire and_1_out, and_2_out, or_1_out, xor_1_out;

  or or_1 (or_1_out, C, B);
  xor xor_1 (xor_1_out, C, B);
  and and_1 (and_1_out, or_1_out, A);
  and and_2 (and_2_out, C, B);
  xor xor_2 (S, xor_1_out, A);
  or or_2 (Vai_1, and_1_out, and_2_out);
endmodule

module ADD_4 (
  input  [3:0] B,
  input  [3:0] A,
  output Overflow,
  output [3:0] S
);

  wire add_1_2_vai_1, add_1_3_vai_1, add_1_4_vai_1;

  ADD_1 add_1_1 (.S(S[3]), .Vai_1(Overflow), .A(A[3]), .B(B[3]), .C(add_1_2_vai_1));
  ADD_1 add_1_2 (.S(S[2]), .Vai_1(add_1_2_vai_1), .A(A[2]), .B(B[2]), .C(add_1_3_vai_1));
  ADD_1 add_1_3 (.S(S[1]), .Vai_1(add_1_3_vai_1), .A(A[1]), .B(B[1]), .C(add_1_4_vai_1));
  ADD_1 add_1_4 (.S(S[0]), .Vai_1(add_1_4_vai_1), .A(A[0]), .B(B[0]), .C(1'b0));
endmodule

module SUB_1 (
  input  A,
  input  B,
  input  C,
  output S,
  output Vai_1
);

  wire and_1_out, and_2_out, or_1_out, xor_1_out;

  or or_1 (or_1_out, C, B);
  xor xor_1 (xor_1_out, C, B);
  and and_1 (and_1_out, or_1_out, ~A);  // AND_Gate
  and and_2 (and_2_out, C, B);
  xor xor_2 (S, xor_1_out, A);
  or or_2 (Vai_1, and_1_out, and_2_out);
endmodule

module SUB_4 (
  input  [3:0] B,
  input  [3:0] A,
  output Overflow,
  output [3:0] S
);

  wire sub_1_2_vai_1, sub_1_3_vai_1, sub_1_4_vai_1;

  // Probe on A
  SUB_1 sub_1_1 (.S(S[3]), .Vai_1(Overflow), .A(A[3]), .B(B[3]), .C(sub_1_2_vai_1));
  SUB_1 sub_1_2 (.S(S[2]), .Vai_1(sub_1_2_vai_1), .A(A[2]), .B(B[2]), .C(sub_1_3_vai_1));
  SUB_1 sub_1_3 (.S(S[1]), .Vai_1(sub_1_3_vai_1), .A(A[1]), .B(B[1]), .C(sub_1_4_vai_1));
  // Probe on S
  SUB_1 sub_1_4 (.S(S[0]), .Vai_1(sub_1_4_vai_1), .A(A[0]), .B(B[0]), .C(1'b0));
  // Probe on B
endmodule

module Rot_esq (
  input  [3:0] a_b_c_d,
  input  [1:0] x_y,
  output [3:0] A__B_C_D
);

  wire and_1_out, and_2_out, and_3_out, and_4_out, and_5_out, and_6_out, and_7_out, and_8_out, and_9_out;

  and and_1 (and_1_out, ~x_y[1], ~x_y[0], a_b_c_d[3]);  // AND_Gate
  and and_2 (and_2_out, ~x_y[1], x_y[0], a_b_c_d[2]);  // AND_Gate
  and and_3 (and_3_out, x_y[1], ~x_y[0], a_b_c_d[1]);  // AND_Gate
  and and_4 (and_4_out, x_y[1], x_y[0], a_b_c_d[0]);
  and and_5 (and_5_out, ~x_y[1], ~x_y[0], a_b_c_d[2]);  // AND_Gate
  and and_6 (and_6_out, ~x_y[1], x_y[0], a_b_c_d[1]);  // AND_Gate
  and and_7 (and_7_out, x_y[1], ~x_y[0], a_b_c_d[0]);  // AND_Gate
  and and_8 (and_8_out, ~x_y[1], ~x_y[0], a_b_c_d[1]);  // AND_Gate
  and and_9 (and_9_out, ~x_y[1], x_y[0], a_b_c_d[0]);  // AND_Gate
  and and_10 (A__B_C_D[0], ~x_y[1], ~x_y[0], a_b_c_d[0]);  // AND_Gate
  or or_1 (A__B_C_D[3], and_1_out, and_2_out, and_3_out, and_4_out);
  or or_2 (A__B_C_D[2], and_5_out, and_6_out, and_7_out);
  or or_3 (A__B_C_D[1], and_8_out, and_9_out);
endmodule

module Rot_dir (
  input  [3:0] a_b_c_d,
  input  [1:0] in_2,
  output [3:0] A_B_C_D_2
);

  wire and_1_out, and_2_out, and_3_out, and_4_out, and_5_out, and_6_out, and_7_out, and_8_out, and_9_out;

  and and_1 (and_1_out, ~in_2[1], ~in_2[0], a_b_c_d[0]);  // AND_Gate
  and and_2 (and_2_out, ~in_2[1], in_2[0], a_b_c_d[1]);  // AND_Gate
  and and_3 (and_3_out, in_2[1], ~in_2[0], a_b_c_d[2]);  // AND_Gate
  and and_4 (and_4_out, in_2[1], in_2[0], a_b_c_d[3]);
  and and_5 (and_5_out, ~in_2[1], ~in_2[0], a_b_c_d[1]);  // AND_Gate
  and and_6 (and_6_out, ~in_2[1], in_2[0], a_b_c_d[2]);  // AND_Gate
  and and_7 (and_7_out, in_2[1], ~in_2[0], a_b_c_d[3]);  // AND_Gate
  and and_8 (and_8_out, ~in_2[1], ~in_2[0], a_b_c_d[2]);  // AND_Gate
  and and_9 (and_9_out, ~in_2[1], in_2[0], a_b_c_d[3]);  // AND_Gate
  and and_10 (A_B_C_D_2[3], ~in_2[1], ~in_2[0], a_b_c_d[3]);  // AND_Gate
  or or_1 (A_B_C_D_2[0], and_1_out, and_2_out, and_3_out, and_4_out);
  or or_2 (A_B_C_D_2[1], and_5_out, and_6_out, and_7_out);
  or or_3 (A_B_C_D_2[2], and_8_out, and_9_out);
endmodule
